// Logisim project 4biyt.circ as structural Verilog: 3 circuits, main circuit main
module main (
);

  wire Asel, Clock, decoder_1_out0, decoder_1_out1, EX, register_2_q, Reset, StoreA, StoreD, StoreIR, StoreM,
       StorePC;
  wire [1:0] Op, register_1_q, rom_1_data;
  wire [2:0] R1sel, R2sel;
  wire [3:0] multiplexer_1_out;
  wire [7:0] alu_1_address, alu_1_data, IR, register_3_q, register_4_q, register_5_q, rom_2_data;
  wire [31:17] rom_1_data_2;

  Button u_Reset (.out(Reset));
  Clock clock_1 (.out(Clock));
  Register #(.width(2)) register_1 (.D(rom_1_data), .Q(register_1_q), .clk(Clock), .clr(Reset));  // open: en
  Register #(.width(1)) register_2 (.D(EX), .Q(register_2_q), .clk(Clock), .clr(Reset));  // open: en
  Register register_3 (.D(alu_1_data), .en(StoreD), .Q(register_3_q), .clk(Clock), .clr(Reset));
  Multiplexer #(.width(4), .enable("false")) multiplexer_1 (
    .in0(4'b0000), .in1(IR[3:0]), .out(multiplexer_1_out), .sel(register_2_q));
  ALU alu_1 (
    .Aasel(Asel), .R1sel(R1sel), .R2sel(R2sel), .Op(Op), .A(register_4_q), .PC(register_5_q),
    .D(register_3_q), .M(rom_2_data), .IR(IR), .ADDRESS(alu_1_address), .DATA(alu_1_data));
  Register register_4 (.D(alu_1_data), .en(StoreA), .Q(register_4_q), .clk(Clock), .clr(Reset));
  ROM #(.addrWidth(6), .dataWidth(32)) rom_1 (
    .addr({multiplexer_1_out, register_1_q}),
    .data({rom_1_data_2, EX, StoreM, StoreIR, StorePC, StoreA, StoreD, Op, R2sel, R1sel, Asel, rom_1_data}));  // open: sel
  Register register_5 (.D(alu_1_data), .en(StorePC), .Q(register_5_q), .clk(Clock), .clr(Reset));
  RAM Ram (
    .Address(alu_1_address), .Select(decoder_1_out1), .Clock(Clock), .Write(StoreM), .Reset(Reset),
    .DataIn(alu_1_data), .DataOut(rom_2_data));
  Decoder decoder_1 (.out0(decoder_1_out0), .out1(decoder_1_out1), .sel(alu_1_address[7]));  // open: en
  Register register_6 (.D(alu_1_data), .en(StoreIR), .Q(IR), .clk(Clock), .clr(Reset));
  ROM rom_2 (.addr(alu_1_address), .data(rom_2_data), .sel(decoder_1_out0));

  // Notes on the sheet:
  //   Registers
  //   Data Bus
  //   Microcode ROM
  //   Address Bus
  //   contents of rom_1 (hex, n*v repeats v):
  //   415d 12188 10000 0 108ed 2188 0 0 110ed 2188 0 0 828 0 0 0 10a8 0 0 0 880 0 0 0 20ec 0 0 0 27d0 0 0
  //   0 26b8 0 0 0 1089d 2188 0 0 80a8 0 0 0 10e8 0 0 0 80d0 0 0 0 8d0
  //   contents of rom_2 (hex, n*v repeats v):
  //   2 2 9 1 58 1 0 6
  //   Control Bus
endmodule

module ALU (
  input  [7:0] A,
  input  [7:0] PC,
  input  [7:0] D,
  input  [7:0] M,
  input  [7:0] IR,
  input  Aasel,
  input  [2:0] R1sel,
  input  [2:0] R2sel,
  input  [1:0] Op,
  output [7:0] ADDRESS,
  output [7:0] DATA
);

  wire comparator_1_gt;
  wire [7:0] adder_1_out, multiplexer_2_out, multiplexer_3_out, multiplexer_5_out, not_1_out, shifter_1_out,
       shifter_2_out;

  Multiplexer #(.width(8)) multiplexer_1 (.in0(A), .in1(PC), .out(ADDRESS), .sel(Aasel));  // open: en
  Multiplexer #(.select(3), .width(8)) multiplexer_2 (
    .in0(A), .in1(PC), .in2(D), .in3(M), .in4(IR), .in5({8{1'b0}}), .in6(8'h1), .in7(shifter_2_out),
    .out(multiplexer_2_out), .sel(R1sel));  // open: en
  Adder adder_1 (.a(multiplexer_2_out), .b(multiplexer_3_out), .out(adder_1_out));  // open: cin, cout
  Shifter #(.shift("lr")) shifter_1 (.in(multiplexer_2_out), .\dist (multiplexer_3_out[2:0]), .out(shifter_1_out));
  assign not_1_out = ~multiplexer_2_out;  // NOT_Gate not_1, 8 bits wide
  Multiplexer #(.select(3), .width(8)) multiplexer_3 (
    .in0(A), .in1(PC), .in2(D), .in3(M), .in4(IR), .in5({8{1'b0}}), .in6(8'h1), .in7(shifter_2_out),
    .out(multiplexer_3_out), .sel(R2sel));  // open: en
  Comparator comparator_1 (.a(multiplexer_2_out), .b(multiplexer_3_out), .gt(comparator_1_gt));  // open: eq, lt
  Multiplexer #(.select(2), .width(8)) multiplexer_4 (
    .in0(adder_1_out), .in1(shifter_1_out), .in2(not_1_out), .in3(multiplexer_5_out), .out(DATA), .sel(Op));  // open: en
  Multiplexer #(.width(8)) multiplexer_5 (
    .in0(PC), .in1(A), .out(multiplexer_5_out), .sel(comparator_1_gt));  // open: en
  Shifter #(.shift("lr")) shifter_2 (.in(IR), .\dist (3'b100), .out(shifter_2_out));
endmodule

module RAM (
  input  [7:0] Address,
  input  Select,
  input  Clock,
  input  Write,
  input  Reset,
  input  [7:0] DataIn,
  input  [7:0] DataOut
);

  wire not_1_out;

  assign DataOut = Write ? DataIn : 8'bz;  // Controlled_Buffer controlled_buffer_1
  not not_1 (not_1_out, Write);
  RAM_part ram_1 (.addr(Address), .data(DataOut), .sel(Select), .clk(Clock), .ld(not_1_out), .clr(Reset));
endmodule
