// Logisim project LogisimExperiments.circ as structural Verilog: 1 circuit, main circuit main
module main (
);

  wire [7:0] adder_1_out, controlled_buffer_1_out, controlled_buffer_2_out, controlled_buffer_3_out,
       controlled_buffer_4_out, multiplexer_1_out, multiplexer_2_out, register_1_q, register_2_q,
       register_3_q, register_4_q;

  assign controlled_buffer_1_out = 1'b1 ? adder_1_out : 8'bz;  // Controlled_Buffer controlled_buffer_1
  assign controlled_buffer_2_out = 1'b1 ? adder_1_out : 8'bz;  // Controlled_Buffer controlled_buffer_2
  assign controlled_buffer_3_out = 1'b1 ? adder_1_out : 8'bz;  // Controlled_Buffer controlled_buffer_3
  assign controlled_buffer_4_out = 1'b1 ? adder_1_out : 8'bz;  // Controlled_Buffer controlled_buffer_4
  Register register_1 (.D(controlled_buffer_1_out), .Q(register_1_q));  // open: en, clk, clr
  Register register_2 (.D(controlled_buffer_2_out), .Q(register_2_q));  // open: en, clk, clr
  Register register_3 (.D(controlled_buffer_3_out), .Q(register_3_q));  // open: en, clk, clr
  Register register_4 (.D(controlled_buffer_4_out), .Q(register_4_q));  // open: en, clk, clr
  Multiplexer #(.select(3), .width(8)) multiplexer_1 (
    .in2(register_1_q), .in3(register_2_q), .in4(register_3_q), .in5(register_4_q), .in6(8'h6f),
    .out(multiplexer_1_out), .sel(3'b110));  // open: in0, in1, in7, en
  Multiplexer #(.select(3), .width(8)) multiplexer_2 (
    .in1(register_1_q), .in2(register_2_q), .in3(register_3_q), .in5(register_4_q), .in6(8'h6f),
    .out(multiplexer_2_out), .sel(3'b110));  // open: in0, in4, in7, en
  Adder adder_1 (.a(multiplexer_1_out), .b(multiplexer_2_out), .out(adder_1_out));  // open: cin, cout
endmodule
