// Logisim project hw5.circ as structural Verilog: 4 circuits, main circuit main
module main (
  output cout
);

  wire clock_out, instruction_decoder_1_alu_d0, instruction_decoder_1_alu_d1, instruction_decoder_1_led,
       instruction_decoder_1_sc0, instruction_decoder_1_sc1;
  wire [1:0] instruction_decoder_1_mux, instruction_decoder_1_wsel;
  wire [3:0] alu_1_s0, conter_q, controlled_buffer_1_out, instruction_decoder_1_imm, multiplexer_1_out,
       stack_1_debug, stack_1_top, stack_1_top_1;
  wire [7:0] rom_1_data;

  Clock clock (.out(clock_out));
  Counter #(.width(4), .max('hf)) conter (.Q(conter_q), .clk(clock_out));  // open: load, D, count, carry, clr
  ROM #(.addrWidth(4)) rom_1 (.addr(conter_q), .data(rom_1_data));  // open: sel
  Instruction_Decoder instruction_decoder_1 (
    .instruction(rom_1_data), .Mux(instruction_decoder_1_mux), .sc0(instruction_decoder_1_sc0),
    .sc1(instruction_decoder_1_sc1), .wsel(instruction_decoder_1_wsel),
    .ALU_d0(instruction_decoder_1_alu_d0), .ALU_d1(instruction_decoder_1_alu_d1),
    .LED(instruction_decoder_1_led), .Imm(instruction_decoder_1_imm));
  Multiplexer #(.select(2), .width(4), .enable("false")) multiplexer_1 (
    .in0(alu_1_s0), .in1(stack_1_top), .in2(instruction_decoder_1_imm), .out(multiplexer_1_out),
    .sel(instruction_decoder_1_mux));  // open: in3
  Stack stack_1 (
    .sc0(instruction_decoder_1_sc0), .sc1(instruction_decoder_1_sc1), .write(multiplexer_1_out),
    .w_sel(instruction_decoder_1_wsel), .clock(clock_out), .top(stack_1_top), .top_1(stack_1_top_1),
    .debug(stack_1_debug));
  // Probe on instruction_decoder_1_mux
  // Probe on stack_1_debug
  // Probe on instruction_decoder_1_sc1
  // Probe on instruction_decoder_1_sc0
  ALU alu_1 (
    .c_out(cout), .b3(stack_1_top_1[3]), .b2(stack_1_top_1[2]), .b1(stack_1_top_1[1]), .b0(stack_1_top_1[0]),
    .a3(stack_1_top[3]), .a2(stack_1_top[2]), .a1(stack_1_top[1]), .a0(stack_1_top[0]), .s3(alu_1_s0[3]),
    .s2(alu_1_s0[2]), .s1(alu_1_s0[1]), .s0(alu_1_s0[0]), .d0(instruction_decoder_1_alu_d0),
    .d1(instruction_decoder_1_alu_d1));
  // Probe on instruction_decoder_1_wsel
  // Probe on instruction_decoder_1_alu_d1
  // Probe on instruction_decoder_1_alu_d0
  // Probe on instruction_decoder_1_led
  DotMatrix #(.matrixcols(4), .matrixrows(1), .dotshape("circle")) dotmatrix_1 (
    .col0(controlled_buffer_1_out[3]), .col1(controlled_buffer_1_out[2]), .col2(controlled_buffer_1_out[1]),
    .col3(controlled_buffer_1_out[0]));
  assign controlled_buffer_1_out = instruction_decoder_1_led ? stack_1_top : 4'bz;  // Controlled_Buffer controlled_buffer_1
  // Probe on instruction_decoder_1_imm

  // Notes on the sheet:
  //   CMSC 313 Homework 5
  //   revised: 5/13/13 5:11pm
  //   Program
  //   Counter
  //   Program ROM
  //   MUX
  //   00= ALU
  //   01= Stack top
  //   10= Immediate
  //   11= not used
  //   contents of rom_1 (hex, n*v repeats v):
  //   d0 a3 a4 0 a5 10 c0 80 30 0 c0 20 a7 b0 c0 d0
  //   Instruction
  //   Decoder
  //   Stack Control (sc)
  //   00= zero out
  //   01= +1 (pop)
  //   10= no change
  //   11= -1 (push)
  //   Write Select (wsel)
  //   00= current
  //   01= below
  //   10= no write
  //   11= above
  //   stack control
  //   write
  //   wsel
  //   top
  //   top+1
  //   d0
  //   d1
  //   ALU
  //   00= ADD
  //   01= SUB
  //   10= DEC
  //   11= INC
  //   debug
  //   b3 b2 b1 b0
  //   s3    s2    s1    s0
  //   LED
  //   0= OFF
  //   1= ON
  //   a3 a2 a1 a0
  //   LED
endmodule

module Stack (
  input  sc1,
  input  sc0,
  input  [3:0] write,
  input  [1:0] w_sel,
  input  clock,
  output [3:0] debug,
  output [3:0] top,
  output [3:0] top_1
);

  wire and_1_out, and_2_out, decoder_1_out0, decoder_1_out1, decoder_1_out3;
  wire [3:0] demultiplexer_1_out0, demultiplexer_1_out1, demultiplexer_1_out2, demultiplexer_1_out3,
       demultiplexer_1_out4, demultiplexer_1_out5, demultiplexer_1_out6, demultiplexer_1_out7,
       demultiplexer_1_out8, demultiplexer_1_out9, demultiplexer_1_out10, demultiplexer_1_out11,
       demultiplexer_1_out12, demultiplexer_1_out13, demultiplexer_1_out14, demultiplexer_1_out15, st00_q,
       st01_q, st02_q, st03_q, st04_q, st05_q, st06_q, st07_q, st08_q, st09_q, st10_q, st11_q, st12_q,
       st13_q, st14_q, st15_q;

  Demultiplexer #(.select(4), .width(4), .tristate("true")) demultiplexer_1 (
    .out0(demultiplexer_1_out0), .out1(demultiplexer_1_out1), .out2(demultiplexer_1_out2),
    .out3(demultiplexer_1_out3), .out4(demultiplexer_1_out4), .out5(demultiplexer_1_out5),
    .out6(demultiplexer_1_out6), .out7(demultiplexer_1_out7), .out8(demultiplexer_1_out8),
    .out9(demultiplexer_1_out9), .out10(demultiplexer_1_out10), .out11(demultiplexer_1_out11),
    .out12(demultiplexer_1_out12), .out13(demultiplexer_1_out13), .out14(demultiplexer_1_out14),
    .out15(demultiplexer_1_out15), .in(write), .sel(debug), .en(decoder_1_out3));
  Demultiplexer #(.select(4), .width(4), .tristate("true")) demultiplexer_2 (
    .out0(demultiplexer_1_out1), .out1(demultiplexer_1_out2), .out2(demultiplexer_1_out3),
    .out3(demultiplexer_1_out4), .out4(demultiplexer_1_out5), .out5(demultiplexer_1_out6),
    .out6(demultiplexer_1_out7), .out7(demultiplexer_1_out8), .out8(demultiplexer_1_out9),
    .out9(demultiplexer_1_out10), .out10(demultiplexer_1_out11), .out11(demultiplexer_1_out12),
    .out12(demultiplexer_1_out13), .out13(demultiplexer_1_out14), .out14(demultiplexer_1_out15),
    .out15(demultiplexer_1_out0), .in(write), .sel(debug), .en(decoder_1_out0));
  Decoder #(.select(2), .enable("false")) decoder_1 (
    .out0(decoder_1_out0), .out1(decoder_1_out1), .out3(decoder_1_out3), .sel(w_sel));  // open: out2
  Demultiplexer #(.select(4), .width(4), .tristate("true")) demultiplexer_3 (
    .out0(demultiplexer_1_out2), .out1(demultiplexer_1_out3), .out2(demultiplexer_1_out4),
    .out3(demultiplexer_1_out5), .out4(demultiplexer_1_out6), .out5(demultiplexer_1_out7),
    .out6(demultiplexer_1_out8), .out7(demultiplexer_1_out9), .out8(demultiplexer_1_out10),
    .out9(demultiplexer_1_out11), .out10(demultiplexer_1_out12), .out11(demultiplexer_1_out13),
    .out12(demultiplexer_1_out14), .out13(demultiplexer_1_out15), .out14(demultiplexer_1_out0),
    .out15(demultiplexer_1_out1), .in(write), .sel(debug), .en(decoder_1_out1));
  Register #(.width(4)) st00 (.D(demultiplexer_1_out1), .Q(st00_q), .clk(clock));  // open: en, clr
  Register #(.width(4)) st02 (.D(demultiplexer_1_out3), .Q(st02_q), .clk(clock));  // open: en, clr
  Register #(.width(4)) st04 (.D(demultiplexer_1_out5), .Q(st04_q), .clk(clock));  // open: en, clr
  Register #(.width(4)) st06 (.D(demultiplexer_1_out7), .Q(st06_q), .clk(clock));  // open: en, clr
  Register #(.width(4)) st08 (.D(demultiplexer_1_out9), .Q(st08_q), .clk(clock));  // open: en, clr
  Register #(.width(4)) st10 (.D(demultiplexer_1_out11), .Q(st10_q), .clk(clock));  // open: en, clr
  Register #(.width(4)) st12 (.D(demultiplexer_1_out13), .Q(st12_q), .clk(clock));  // open: en, clr
  Register #(.width(4)) st14 (.D(demultiplexer_1_out15), .Q(st14_q), .clk(clock));  // open: en, clr
  Register #(.width(4)) st01 (.D(demultiplexer_1_out2), .Q(st01_q), .clk(clock));  // open: en, clr
  Register #(.width(4)) st03 (.D(demultiplexer_1_out4), .Q(st03_q), .clk(clock));  // open: en, clr
  Register #(.width(4)) st05 (.D(demultiplexer_1_out6), .Q(st05_q), .clk(clock));  // open: en, clr
  Register #(.width(4)) st07 (.D(demultiplexer_1_out8), .Q(st07_q), .clk(clock));  // open: en, clr
  Register #(.width(4)) st09 (.D(demultiplexer_1_out10), .Q(st09_q), .clk(clock));  // open: en, clr
  Register #(.width(4)) st11 (.D(demultiplexer_1_out12), .Q(st11_q), .clk(clock));  // open: en, clr
  Register #(.width(4)) st13 (.D(demultiplexer_1_out14), .Q(st13_q), .clk(clock));  // open: en, clr
  Register #(.width(4)) st15 (.D(demultiplexer_1_out0), .Q(st15_q), .clk(clock));  // open: en, clr
  and and_1 (and_1_out, sc1, sc0);
  Counter #(.width(4), .max('hf)) counter_1 (
    .load(and_1_out), .count(sc0), .Q(debug), .clk(clock), .clr(and_2_out));  // open: D, carry
  and and_2 (and_2_out, ~sc1, ~clock, ~sc0);  // AND_Gate
  Multiplexer #(.select(4), .width(4), .enable("false")) multiplexer_1 (
    .in0(st00_q), .in1(st01_q), .in2(st02_q), .in3(st03_q), .in4(st04_q), .in5(st05_q), .in6(st06_q),
    .in7(st07_q), .in8(st08_q), .in9(st09_q), .in10(st10_q), .in11(st11_q), .in12(st12_q), .in13(st13_q),
    .in14(st14_q), .in15(st15_q), .out(top), .sel(debug));
  Multiplexer #(.select(4), .width(4), .enable("false")) multiplexer_2 (
    .in0(st01_q), .in1(st02_q), .in2(st03_q), .in3(st04_q), .in4(st05_q), .in5(st06_q), .in6(st07_q),
    .in7(st08_q), .in8(st09_q), .in9(st10_q), .in10(st11_q), .in11(st12_q), .in12(st13_q), .in13(st14_q),
    .in14(st15_q), .in15(st00_q), .out(top_1), .sel(debug));

  // Notes on the sheet:
  //   5 4 3 2 1 0 9 8 7 6 5 4 3 2 1 0
  //   5 4 3 2 1 0 9 8 7 6 5 4 3 2 1 0
endmodule

module Instruction_Decoder (
  input  [7:0] instruction,
  output [1:0] Mux,
  output sc0,
  output sc1,
  output [1:0] wsel,
  output ALU_d0,
  output ALU_d1,
  output LED,
  output [3:0] Imm
);


  assign Imm = instruction[3:0];
endmodule

// 4-bit ALU
module ALU (
  input  b3,
  input  b2,
  input  b1,
  input  b0,
  input  a3,
  input  a2,
  input  a1,
  input  a0,
  input  d0,
  input  d1,
  output c_out,
  output s3,
  output s2,
  output s1,
  output s0
);

  wire [3:0] adder_1_out, adder_2_out, subtractor_1_out, subtractor_2_out;

  Adder #(.width(4)) adder_1 (
    .a({a3, a2, a1, a0}), .b({b3, b2, b1, b0}), .out(adder_1_out), .cout(c_out));  // open: cin
  Subtractor #(.width(4)) subtractor_1 (
    .a({b3, b2, b1, b0}), .b({a3, a2, a1, a0}), .out(subtractor_1_out));  // open: bin, bout
  Subtractor #(.width(4)) subtractor_2 (.a({a3, a2, a1, a0}), .b(4'b0001), .out(subtractor_2_out));  // open: bin, bout
  Multiplexer #(.select(2), .width(4), .enable("false")) multiplexer_1 (
    .in0(adder_1_out), .in1(subtractor_1_out), .in2(subtractor_2_out), .in3(adder_2_out),
    .out({s3, s2, s1, s0}), .sel({d1, d0}));
  Adder #(.width(4)) adder_2 (.a({a3, a2, a1, a0}), .b(4'b0001), .out(adder_2_out));  // open: cin, cout

  // Notes on the sheet:
  //   a3-a0
  //   b3-b0
endmodule
