// Logisim project lecture18.circ as structural Verilog: 1 circuit, main circuit main
module main (
  input  in_1,
  input  in_2,
  input  in_3,
  input  in_4,
  input  Data,
  input  in_6,
  input  in_7,
  input  Store
);

  wire button_1_out, button_2_out, nand_1_out, nand_2_out, nand_3_out, nand_4_out, nand_5_out, nand_6_out,
       nand_7_out, nand_8_out, nand_9_out, nand_10_out, transistor_1_out, transistor_2_out, transistor_4_out;

  Button button_1 (.out(button_1_out));
  Button button_2 (.out(button_2_out));
  nand nand_1 (nand_1_out, Data, Store);
  nand nand_2 (nand_2_out, nand_1_out, Store);
  Transistor transistor_1 (.in(1'b1), .out(transistor_1_out), .gate(button_1_out));
  LED led_1 (.in(transistor_1_out));
  nand nand_3 (nand_3_out, button_2_out, button_2_out);
  LED led_2 (.in(nand_3_out));
  nand nand_4 (nand_4_out, nand_1_out, nand_5_out);
  nand nand_5 (nand_5_out, nand_4_out, nand_2_out);
  LED led_3 (.in(nand_4_out));
  Transistor transistor_2 (.in(1'b1), .out(transistor_2_out), .gate(in_1));
  Transistor #(.\type ("n")) transistor_3 (.in(transistor_4_out), .out(transistor_2_out), .gate(in_1));
  Transistor #(.\type ("n")) transistor_4 (.in(1'b0), .out(transistor_4_out), .gate(in_2));
  nand nand_6 (nand_6_out, in_3, in_3);
  nand nand_7 (nand_7_out, in_4, in_4);
  Transistor transistor_5 (.in(1'b1), .out(transistor_2_out), .gate(in_2));
  nand nand_8 (nand_8_out, nand_6_out, nand_7_out);
  nand nand_9 (nand_9_out, in_6, nand_10_out);
  nand nand_10 (nand_10_out, nand_9_out, in_7);
  LED led_4 (.in(nand_8_out));
  LED led_5 (.in(nand_9_out));
  // Probe on transistor_2_out

  // Notes on the sheet:
  //   P-type Transistors conduct when the base is at low potential
  //   This is a NOT Gate
  //   NAND can be used to create any other gate
  //   This is a NOT gate
  //   With feedback, we can even create Flip-Flops using NAND
  //   This is a one-bit register
  //   Transistors can be combined to perform other logical operations
  //   This is a NAND gate
  //   We can use DeMorgan's Law to go from A || B to !(!A && !B)
  //   And here's OR
endmodule
