// Logisim project parity.circ as structural Verilog: 1 circuit, main circuit main
module main (
  input  A,
  input  B,
  input  C
);

  wire and_1_out, and_2_out, and_3_out, and_4_out, not_1_out, not_2_out, not_3_out, or_1_out, undriven,
       undriven_2, undriven_3;

  not not_1 (not_1_out, undriven);
  not not_2 (not_2_out, undriven_2);
  not not_3 (not_3_out, undriven_3);
  // AND_Gate and_1 has open pins: out=and_1_out
  // AND_Gate and_2 has open pins: out=and_2_out
  // AND_Gate and_3 has open pins: out=and_3_out
  // AND_Gate and_4 has open pins: out=and_4_out
  or or_1 (or_1_out, and_1_out, and_2_out, and_3_out, and_4_out);

  // Notes on the sheet:
  //   Out
endmodule
